# Fritzing sketch grove_capa (saved by Fritzing 0.9.4)

parts:
  R1 = Resistor [tolerance=±0.1% resistance=10k package=THT]  # not connected
  J1 = female pin header, 1 pin [form="♀ (female)"]
  J2 = female pin header, 1 pin [form="♀ (female)"]
  C1 = Ceramic Capacitor [capacitance=100nF package="100 mil [THT, multilayer]"]

nets:
  N1: J1.pin1, C1.0
  N2: J2.pin1, C1.1

notes:
  Connecteur Grove
  (Sortie digitale) A0
  (Entrée analogique) A1
  (Non connecté) VCC
  GND
  10k
