# Fritzing sketch microbit_BP_pull_up (saved by Fritzing 0.9.4)

parts:
  Mod1 = Microbit
  S4 = Pushbutton [package=THT]
  R1 = Resistor [tolerance=±5% resistance=10k package=THT]

nets:
  N1: Mod1.3V3, R1.Pin_0
  N2: Mod1.GND, S4.leg0
  N3: S4.leg1, R1.Pin_1

notes:
  Bouton poussoir
  10 k
  0 (fermé) - 1 (ouvert)

custom parts:
  Microbit: BBC Microbit Fritzing part. May 2019 expanded to include schematic and pcb views as well as breadboard. PCB view assumes an Adafruit PRODUCT ID: 3342 2x40 Right Angle through hole edge connector (although others will probably work as well). The pcb svg is custom (see forum article http://forum.fritzing.org/t/making-edge-connectors-and-both-side-smd-parts/7287 for an explaination if you need to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
