# Fritzing sketch microbit_potentiometre (saved by Fritzing 0.9.4)

parts:
  Mod1 = Microbit
  RE1 = Rotary Encoder [package=THT]

nets:
  N1: Mod1.P0, RE1.EncoderPinC
  N2: Mod1.3V3, RE1.EncoderPinB
  N3: Mod1.GND, Mod1.Bat_-, RE1.EncoderPinA

notes:
  3,3 V
  0 V
  0 à 3,3 V

custom parts:
  Microbit: BBC Microbit Fritzing part. May 2019 expanded to include schematic and pcb views as well as breadboard. PCB view assumes an Adafruit PRODUCT ID: 3342 2x40 Right Angle through hole edge connector (although others will probably work as well). The pcb svg is custom (see forum article http://forum.fritzing.org/t/making-edge-connectors-and-both-side-smd-parts/7287 for an explaination if you need to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
