# Fritzing sketch nucleo_dfu_bootloader_mode (saved by Fritzing 0.9.4)

parts:
  J1 = STM32 Nucleo boards
  USBTTL1 = USB TTL Serial Cable

nets:
  N1: J1.PA12, USBTTL1.RX
  N2: J1.PA11, USBTTL1.TX
  N3: J1.E5V, USBTTL1.5V
  GND: J1.GND, USBTTL1.GND
  N4: J1.VDD, J1.BOOT0

notes:
  Mode DFU
  D+
  D-
  5 V
  0 V
  Cable USB
