# Fritzing sketch pyboard_dfu_bootloader_mode (saved by Fritzing 0.9.4)

parts:
  pyboard1 = Micro Python pyboard [part_number=PYBv10b]

nets:
  N1: pyboard1.P1_BOOT0, pyboard1.X15_3V3

notes:
  Mode DFU Bootloader
