# Fritzing sketch pyboard_v11_bp_intern_pull_up_resistor (saved by Fritzing 0.9.4)

parts:
  pyboard1 = Micro Python pyboard [part_number=PYBv10b]
  S1 = Pushbutton [package=THT]

nets:
  N1: pyboard1.P9A_GND, S1.leg0
  N2: pyboard1.X5, S1.leg1

notes:
  0 V (fermé)
  0 V
  3,3 V (ouvert)
  BP
