# Fritzing sketch pyboard_v11_dac_voltmeter (saved by Fritzing 0.9.4)

parts:
  pyboard1 = Micro Python pyboard [part_number=PYBv10b]
  Voltmeter1 = Voltmeter

nets:
  N1: pyboard1.X5, Voltmeter1.Positive
  N2: pyboard1.Y14_GND, Voltmeter1.Com

custom parts:
  Voltmeter: A Standard Multimeter in Current mode
