# Fritzing sketch pyboard_v11_led_X6 (saved by Fritzing 0.9.4)

parts:
  pyboard1 = Micro Python pyboard [part_number=PYBv10b]
  R1 = Resistor [tolerance=±5% resistance=220 package=THT]
  LED1 = LED - 5mm [color="Red (633nm)" package="5 mm [THT]"]

nets:
  N1: pyboard1.X6, R1.Pin_0
  N2: pyboard1.Y14_GND, LED1.cathode
  N3: R1.Pin_1, LED1.anode

notes:
  220
  LED
  0 V
  X6
