# Fritzing sketch pyboard_v11_potentiometer (saved by Fritzing 0.9.4)

parts:
  pyboard1 = Micro Python pyboard [part_number=PYBv10b]
  R1 = Rotary Potentiometer (Small) [maximum_resistance=100kΩ package=THT]

nets:
  N1: pyboard1.P9A_GND, R1.leg2
  N2: pyboard1.X5, R1.wiper
  N3: pyboard1.Y15_3V3, R1.leg1

notes:
  3,3 V
  0 V
  Potentiomètre
  0 à 3,3 V
